# Fritzing sketch ESP-01_deepSleep (saved by Fritzing 0.8.3b)
breadboards: 1

parts:
  U2 = ESP8266 WiFi Module [part_number=ESP8266]
  S1 = Pushbutton [package="[THT]"]
  Power_plug1 = Power plug

nets:
  VCC: U2.VCC, U2.CH_PD, S1.Pin_3, S1.Pin_4, Power_plug1.VCC
  N1: U2.RST, S1.Pin_1, S1.Pin_2
  GND: U2.GND, Power_plug1.GND

notes:
  3.3V Power in

custom parts:
  ESP8266 WiFi Module: Generic WiFi Module based on the ESP8266 with onboard PCB antenna and UART communications
