# Fritzing sketch ESP-07_deepSleep (saved by Fritzing 0.8.3b)
breadboards: 1

parts:
  Power_plug1 = Power plug
  U1 = ESP8266 WiFi Module [part_number=ESP8266]

nets:
  GND: Power_plug1.GND, U1.GND, U1.GPIO_15
  VCC: Power_plug1.VCC, U1.VCC, U1.CH_PD
  N1: U1.GPIO_16, U1.REST

notes:
  3.3V Power in
