# Fritzing sketch RelayBuildLayout (saved by Fritzing 0.8.3b)
breadboards: 1

parts:
  U1 = ESP8266 WiFi Module [part_number=ESP8266]
  C1 = Ceramic Capacitor [capacitance=100nF package="100 mil [THT, multilayer]"]  # not connected
  C2 = Electrolytic Capacitor [capacitance=100µF voltage=16V package="100 mil [THT, electrolytic]"]  # not connected
  Power_plug1 = Power plug
  HLK-PM1 = HLK-PM01
  Part1 = Adafruit LM3671 Buck Converter [part_number="Adafruit #2745"]
  KY-1 = Keyes Relay [package=THT]
  R1 = Resistor [tolerance=±5% resistance=220 package=THT]
  S1 = Pushbutton [package="[THT]"]
  R2 = Resistor [tolerance=±5% resistance=220 package=THT]
  C3 = Electrolytic Capacitor [capacitance=1µF package="100 mil [THT, electrolytic]"]  # not connected

nets:
  N1: U1.RXD, R1.Pin_1
  VCC: U1.VCC, U1.CH_PD, Part1.3.3V, R2.Pin_1
  N2: U1.GPIO_0, S1.Pin_3, S1.Pin_4
  GND: U1.GND, HLK-PM1.-Vo, Part1.GND, KY-1.ground
  N3: Power_plug1.GND, HLK-PM1.AC, KY-1.NO
  N4: HLK-PM1.+Vo, Part1.VIN, KY-1.power
  N5: KY-1.signal, R1.Pin_0
  N6: S1.Pin_1, S1.Pin_2, R2.Pin_0

notes:
  AC in
  Couldnt find my buck
  converter in fritzing but this
  is the same thing effectivly
  AC to DC converter
  Hot and Neutral lines that
  go to the load (Lights, Fans, etc.)

custom parts:
  ESP8266 WiFi Module: Generic WiFi Module based on the ESP8266 with onboard PCB antenna and UART communications
  Adafruit LM3671 Buck Converter: Your power supply problems just got SUPER SOLVED! This 3.3V Buck Converter Breakout board is great for supplying power to low voltage circuits from a single Li-Ion cell battery or USB power. This chip provides up to 600-mA load current across the entire input voltage range of 3.5 to 5.5V. Great for your portable project, we made this "pin compatible" with the LM1117-3.3V TO-220 chip so you can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
  Keyes Relay: The Keyes 5V relay module is suitable for SCM development, home appliance control. It uses a 5V~12V TIL control signal which can control DC / AC signal.
